# Fritzing sketch Washer-Dryer (saved by Fritzing 0.9.3b)
stripboards: 1

parts:
  U1 = NodeMCU V3.0
  R1 = Resistor [tolerance=±5% resistance=10k package=THT]
  R2 = Resistor [tolerance=±5% resistance=10k package=THT]
  C1 = Electrolytic Capacitor [capacitance=10µF voltage=10V package="100 mil [THT, electrolytic]"]
  U2 = 3.5mm Audio Jack [package=audio-jack-3.5mm-smd]
  GY1 = MPU-6050 Board GY-521 [form="♀ (female)" package=THT]

nets:
  N1: U1.3V3, R1.Pin_0, GY1.pin1
  N2: U1.GND#6, U1.GND#13, U1.GND#16, U1.GND#33, R2.Pin_1, C1.-, GY1.pin2
  N3: U1.D5, GY1.pin8
  N4: U1.D6, GY1.pin3
  N5: U1.D7, GY1.pin4
  N6: U1.A0, U2.RIGHT, U2.LEFT
  N7: R1.Pin_1, R2.Pin_0, C1.+, U2.SLEEVE

notes:
  Washer Dryer Sensor, ESP8266/MPU 6050/Current Sensor, 3.0

custom parts:
  NodeMCU V3.0: ESP8266 based NodeMCU
  MPU-6050 Board GY-521: Acelerometro y Giroscopio MPU-6050 Board GY-521
